# Fritzing sketch schematic-smart-farming (saved by Fritzing 0.9.5d)

parts:
  U1 = LCD-16X2 [package=lcd-16x2_noholes]
  LCM1602_IIC1 = LCM1602 IIC [part_number="LCM1602 IIC" chip_label="LCM1602 IIC" package="DIP (Dual Inline) [THT]"]
  WATER_PUMP1 = water pump/motor  # not connected
  YL-83_-_Detection_Board1 = YL-83 Rain Sensor - Detection Board
  YL-83_-_Control_Board1 = YL-83 Rain Sensor - Control Board
  Capacitive_Soil_Moisture_Sensor1 = DFRobot Capacitive Soil Moisture Sensor V1.0 [part_number=SEN0193]
  DS2 = DS18B20 1-Wire Temperature Sensor Probe
  M1 = 1 chan 5v relay module
  J1 = DHT11 basic temperature-humidity sensor [form="♂ (male)" package=THT]
  U2 = ESP32-38PinWide [part_number=ESP32-38PinWide]
  JACK1 = 2.1mm Barrel Jack with Terminal Block
  A1 = Arduino pluggable terminal

nets:
  VSS: U1.VSS, LCM1602_IIC1.VSS
  VDD: U1.VDD, LCM1602_IIC1.VDD
  N1: U1.VO, LCM1602_IIC1.V0
  N2: U1.RS, LCM1602_IIC1.RS
  N3: U1.R_W, LCM1602_IIC1.RW
  N4: U1.E, LCM1602_IIC1.E
  N5: U1.DB0, LCM1602_IIC1.D0
  N6: U1.DB1, LCM1602_IIC1.D1
  N7: U1.DB2, LCM1602_IIC1.D2
  N8: U1.DB3, LCM1602_IIC1.D3
  N9: U1.DB4, LCM1602_IIC1.D4
  N10: U1.DB5, LCM1602_IIC1.D5
  N11: U1.DB6, LCM1602_IIC1.D6
  N12: U1.DB7, LCM1602_IIC1.D7
  N13: U1.A, LCM1602_IIC1.A
  N14: U1.K, LCM1602_IIC1.K
  N15: LCM1602_IIC1.GND, M1.pin_2, U2.GPIO11
  VCC: LCM1602_IIC1.VCC, M1.pin_1, U2.VIN
  N16: LCM1602_IIC1.SDA, U2.GPIO21
  N17: LCM1602_IIC1.SCL, U2.GPIO22
  N18: YL-83_-_Detection_Board1.POS, YL-83_-_Control_Board1.NEG
  N19: YL-83_-_Detection_Board1.NEG, YL-83_-_Control_Board1.POS
  N20: YL-83_-_Control_Board1.DO, U2.GPIO18
  N21: Capacitive_Soil_Moisture_Sensor1.A, U2.GPIO34
  GND: DS2.GND, J1.GND, U2.GND, A1.Pin_3, A1.Pin_4
  N22: DS2.DQ, U2.GPIO5, A1.Pin_1, A1.Pin_6
  N23: DS2.VDD, A1.Pin_2, A1.Pin_5
  N24: M1.pin_3, U2.GPIO32
  N25: M1.pin_4, JACK1.POS
  N26: J1.VCC, U2.3.3
  N27: J1.OUT, U2.GPIO0, U2.GPIO4

custom parts:
  LCM1602 IIC: I2C-Module to use a 1602 or 2004 LCD on with the wire.h libory Serial LCD Modul
  water pump/motor: WATER PUMP BY ARDUBLOCKTR
  YL-83 Rain Sensor - Detection Board: The YL-83 is a rain sensor that has more resistance when dry and less resistance when wet. The module runs at 5V.
  YL-83 Rain Sensor - Control Board: The YL-83 is a rain sensor that has more resistance when dry and less resistance when wet. The module runs at 5V.
  DFRobot Capacitive Soil Moisture Sensor V1.0: DFRobot Capacitive Soil Moisture Sensor V1.0 This product measures soil moisture levels by capacitive sensing, rather than resistive sensing like other types of moisture sensor. It is made of a corrosion resistant material giving it a long service life. Insert it into soil and impress your friends with the real-time soil moisture data! The product includes an on-board voltage regulator which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
  1 chan 5v relay module: 1 Channel 5V Relay Module Board Shield with Optocoupler Support High and Low Level Trigger for Arduino.
  DHT11 basic temperature-humidity sensor: The DHT11 is a basic, ultra low-cost digital temperature and humidity sensor. It uses a capacitive humidity sensor and a thermistor to measure the surrounding air, and spits out a digital signal on the data pin (no analog input pins needed). Its fairly simple to use, but requires careful timing to grab data. The only real downside of this sensor is you can only get new data from it once every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
  ESP32-38PinWide: Generic 38-Pin ESP32 with wide format (only access to one side of pins on a breadboard) based on Stephen Lilley's HiLetgo ESP-WROOM-32 ESP32 ESP-32S Development Board.
  Arduino pluggable terminal: Arduino pluggable terminal.
